# Fritzing sketch nalle (saved by Fritzing 0.8.5b)
breadboards: 1

parts:
  Part1 = Arduino Uno (Rev3)
  J1 = Piezo Speaker
  R1 = Photocell (LDR) [package=THT]
  J2 = Basic Servo
  J3 = Basic Servo
  LED6 = RGB LED (com. cathode, rgb) [package="5 mm [THT]"]
  LED5 = RGB LED (com. cathode, rgb) [package="5 mm [THT]"]
  R2 = Resistor [tolerance=±5% resistance=220 package=THT]
  R3 = Resistor [tolerance=±5% resistance=220 package=THT]
  R4 = Resistor [tolerance=±5% resistance=220 package=THT]
  R5 = Resistor [tolerance=±5% resistance=220 package=THT]
  R6 = Resistor [tolerance=±10% resistance=220 package=THT]
  R7 = Resistor [tolerance=±5% resistance=220 package=THT]
  R8 = Resistor [tolerance=±5% resistance=220 package=THT]
  S1 = Tilt Switch [package=THT]  # not connected

nets:
  N1: Part1.A0, R1.pin_1, R6.Pin_0
  N2: Part1.D9_PWM, R5.Pin_1
  N3: Part1.D10_PWM/SS, R3.Pin_1
  N4: Part1.D11_PWM/MOSI, R2.Pin_1
  N5: Part1.D12/MISO, J1.pin2
  GND: Part1.GND, J1.pin1, J2.gnd, J3.gnd, LED6.common_cathode, LED5.common_cathode, R6.Pin_1
  N6: Part1.D1/TX, J2.pulse
  N7: Part1.D2, J3.pulse
  N8: Part1.D5_PWM, R4.Pin_1
  N9: Part1.D6_PWM, R8.Pin_1
  N10: Part1.D7, R7.Pin_1
  VCC: Part1.5V, R1.pin_0, J2.vcc, J3.vcc
  N11: LED6.red_anode, R7.Pin_0
  N12: LED6.green_anode, R8.Pin_0
  N13: LED6.blue_anode, R4.Pin_0
  N14: LED5.red_anode, R2.Pin_0
  N15: LED5.green_anode, R3.Pin_0
  N16: LED5.blue_anode, R5.Pin_0
