# Fritzing sketch tassujen_heilutus_tahdissa (saved by Fritzing 0.8.0b)
breadboards: 1

parts:
  Part1 = Arduino Uno (Rev3)
  J1 = Basic Servo
  J2 = Basic Servo
  S1 = Pushbutton [package="[THT]"]
  R1 = Resistor [tolerance=±5% resistance=220 package=THT]

nets:
  N1: Part1.ICSP_MOSI, Part1.D11_PWM/MOSI, S1.Pin_1, S1.Pin_2, R1.Pin_0
  VCC: Part1.5V, J1.vcc, J2.vcc, S1.Pin_3, S1.Pin_4
  GND: Part1.GND, J1.gnd, J2.gnd, R1.Pin_1
  N2: Part1.D9_PWM, J2.pulse
  N3: Part1.D6_PWM, J1.pulse
