# Fritzing sketch nalle_rakennussarja (saved by Fritzing 0.8.5b)
breadboards: 1

parts:
  Part1 = Arduino Uno (Rev3)
  S1 = Tilt Switch [package=THT]
  J1 = Piezo Speaker
  J2 = Basic Servo
  J4 = Basic Servo
  R1 = Photocell (LDR) [package=THT]
  R2 = Resistor [tolerance=±5% resistance=10k package=THT]
  R3 = Resistor [tolerance=±5% resistance=10k package=THT]

nets:
  N1: Part1.A0, R1.pin_0, R3.Pin_1
  N2: Part1.D8, S1.Pin_2, R2.Pin_0
  N3: Part1.D12/MISO, J1.pin2
  GND: Part1.GND, J1.pin1, J2.gnd, J4.gnd, R2.Pin_1, R3.Pin_0
  N4: Part1.D2, J4.pulse
  N5: Part1.D4, J2.pulse
  VCC: Part1.5V, S1.Pin_1, J2.vcc, J4.vcc, R1.pin_1
