# Fritzing sketch ohikulkijalle_vilkutus (saved by Fritzing 0.8.0b)
breadboards: 1

parts:
  Part1 = Arduino Uno (Rev3)
  J1 = Basic Servo
  R1 = Photocell (LDR) [package=THT]
  R2 = Resistor [tolerance=±5% resistance=220 package=THT]

nets:
  N1: Part1.A0, R1.pin_1, R2.Pin_0
  GND: Part1.GND, J1.gnd, R2.Pin_1
  N2: Part1.D6_PWM, J1.pulse
  5V: Part1.5V, J1.vcc, R1.pin_0
