# Fritzing sketch vartoitus_kaatumisesta (saved by Fritzing 0.8.0b)
breadboards: 1

parts:
  Part1 = Arduino Uno (Rev3)
  J1 = Piezo Speaker
  S1 = Tilt Switch [package=THT]
  R2 = Resistor [tolerance=±5% resistance=220 package=THT]
  S6 = Tilt Switch [package=THT]
  R3 = Resistor [tolerance=±5% resistance=220 package=THT]

nets:
  N1: Part1.ICSP_MISO, Part1.D12/MISO, J1.pin2
  N2: Part1.GND, J1.pin1, R2.Pin_1, R3.Pin_1
  N3: Part1.D2, R2.Pin_0, S6.Pin_1
  N4: Part1.D4, S1.Pin_1, R3.Pin_0
  N5: Part1.5V, S1.Pin_2, S6.Pin_2
